# Fritzing sketch Diagrama_del_Circuito (saved by Fritzing 0.9.0b)
breadboards: 1

parts:
  Parte1 = Arduino Uno (Rev3)
  R1 = Resistor [tolerance=±5% resistance=220 package="1206 [SMD]"]
  R2 = Resistor [tolerance=±5% resistance=220 package="1206 [SMD]"]
  R3 = Resistor [tolerance=±5% resistance=220 package="1206 [SMD]"]
  R4 = Resistor [tolerance=±5% resistance=220 package="1206 [SMD]"]
  R5 = Resistor [tolerance=±5% resistance=220 package="1206 [SMD]"]
  LED1 = smd LED [color="Orange (620nm)" package="0805 [SMD]"]
  LED2 = smd LED [color="Orange (620nm)" package="0805 [SMD]"]
  LED3 = smd LED [color="Orange (620nm)" package="0805 [SMD]"]
  LED4 = smd LED [color="Orange (620nm)" package="0805 [SMD]"]
  LED5 = smd LED [color="Orange (620nm)" package="0805 [SMD]"]

nets:
  N1: Parte1.GND, LED1.cathode, LED2.cathode, LED3.cathode, LED4.cathode
  N2: Parte1.D0/RX, R4.Pin_1
  N3: Parte1.D1/TX, R3.Pin_1
  N4: Parte1.D2, R2.Pin_1
  N5: Parte1.D3_PWM, R5.Pin_1
  N6: Parte1.D4, R1.Pin_1
  N7: R1.Pin_0, LED1.anode
  N8: R2.Pin_0, LED3.anode
  N9: R3.Pin_0, LED4.anode
  N10: R4.Pin_0, LED5.anode
  N11: R5.Pin_0, LED2.anode
