# Fritzing sketch Diagrama_del_circuito (saved by Fritzing 0.9.0b)
breadboards: 1

parts:
  Parte1 = Arduino Uno (Rev3)
  S3 = Momentary Switch [package=ksa_sealed_tac_switch]

nets:
  N1: Parte1.GND, S3.4
  N2: Parte1.D2, S3.2
