# Fritzing sketch Diagrama_del_circuito (saved by Fritzing 0.9.0b)
breadboards: 1

parts:
  Parte1 = Arduino Uno (Rev3)
  R1 = TRIMPOT [package=3362u-2]
  LED1 = smd LED [color="Red (633nm)" package="0603 [SMD]"]

nets:
  N1: Parte1.A0, R1.WIPER
  N2: Parte1.GND, R1.CCW, LED1.cathode
  N3: Parte1.D3_PWM, LED1.anode
  N4: Parte1.5V, R1.CW
