# Fritzing sketch Diagrama_del_circuito (saved by Fritzing 0.9.0b)
breadboards: 1

parts:
  Parte1 = Arduino Uno (Rev3)
  S1 = Pushbutton [package="[SMD]"]
  R1 = Resistor [tolerance=±5% resistance=220 package="1206 [SMD]"]
  LED1 = LED - 3mm [color="Red (633nm)" package="3 mm [THT]"]
  R2 = Resistor [tolerance=±5% resistance=220 package="1206 [SMD]"]

nets:
  N1: Parte1.D2, R1.Pin_0
  N2: Parte1.D4, R2.Pin_1
  N3: Parte1.5V, S1.Pin_1, S1.Pin_2
  N4: Parte1.GND, LED1.cathode
  N5: S1.Pin_3, S1.Pin_4, R1.Pin_1
  N6: LED1.anode, R2.Pin_0
