# Fritzing sketch Diagrama_del_circuito (saved by Fritzing 0.9.1b)
breadboards: 1

parts:
  H_E_L_L_O_W_O_R_L_D_!_!_! = LCD screen
  Parte1 = Arduino Uno (Rev3)
  R1 = TRIMPOT [package=3386u]

nets:
  VSS: H_E_L_L_O_W_O_R_L_D_!_!_!.VSS, H_E_L_L_O_W_O_R_L_D_!_!_!.LED-, Parte1.GND, R1.CCW
  VDD: H_E_L_L_O_W_O_R_L_D_!_!_!.VDD, H_E_L_L_O_W_O_R_L_D_!_!_!.LED+, Parte1.5V, R1.CW
  N1: H_E_L_L_O_W_O_R_L_D_!_!_!.V0, R1.WIPER
  N2: H_E_L_L_O_W_O_R_L_D_!_!_!.RS, Parte1.D12/MISO
  N3: H_E_L_L_O_W_O_R_L_D_!_!_!.R/W, Parte1.D10_PWM/SS
  N4: H_E_L_L_O_W_O_R_L_D_!_!_!.E, Parte1.D11_PWM/MOSI
  N5: H_E_L_L_O_W_O_R_L_D_!_!_!.DB4, Parte1.D5_PWM
  N6: H_E_L_L_O_W_O_R_L_D_!_!_!.DB5, Parte1.D4
  N7: H_E_L_L_O_W_O_R_L_D_!_!_!.DB6, Parte1.D3_PWM
  N8: H_E_L_L_O_W_O_R_L_D_!_!_!.DB7, Parte1.D2
