# Fritzing sketch Diagrama_del_circuito (saved by Fritzing 0.9.1b)
circuit board: 8.46667cm x 5.64444cm
breadboards: 1

parts:
  PIR1 = PIR sensor
  Parte1 = Arduino Uno (Rev3) - ICSP
  LED1 = smd LED [color="Red (633nm)" package="0805 [SMD]"]
  R1 = Resistor [tolerance=±5% resistance=220 package=THT]

nets:
  VDD: PIR1.VDD, Parte1.5V
  N1: PIR1.SIG, Parte1.A3
  GND: PIR1.GND, Parte1.GND, LED1.cathode
  N2: Parte1.D2, R1.Pin_1
  N3: LED1.anode, R1.Pin_0
